# Fritzing sketch Googly Eye Clock Sketch (saved by Fritzing 1.0.5)
circuit board: 8.46667cm x 5.64444cm
breadboards: 1

parts:
  Pico/Pico2_Mod_1 = Raspberry Pi Pico or Pico 2
  ZS-042_RTC1 = ZS-042 RTC Module
  Driver1 = 28BYJ-48 Driver Module [part_number=ULN2003 package=THT]
  Driver2 = 28BYJ-48 Driver Module [part_number=ULN2003 package=THT]
  SM1 = 28BYJ-48 Stepper Motor [part_number=28BYJ-48]
  SM2 = 28BYJ-48 Stepper Motor [part_number=28BYJ-48]
  3-pins_Hall_Effect_Sensor1 = mystery part, 3 pins [chip_label="Hall Effect Sensor"]  # not connected

nets:
  N1: Pico/Pico2_Mod_1.pin_3, Pico/Pico2_Mod_1.pin_8, Pico/Pico2_Mod_1.pin_13, Pico/Pico2_Mod_1.pin_18, Pico/Pico2_Mod_1.pin_23, Pico/Pico2_Mod_1.pin_28, Pico/Pico2_Mod_1.pin_33, Pico/Pico2_Mod_1.pin_38, Pico/Pico2_Mod_1.pin_42, ZS-042_RTC1.GND
  N2: Pico/Pico2_Mod_1.pin_6, ZS-042_RTC1.SDA
  N3: Pico/Pico2_Mod_1.pin_7, ZS-042_RTC1.SCL
  N4: Pico/Pico2_Mod_1.pin_9, Driver1.IN1
  N5: Pico/Pico2_Mod_1.pin_10, Driver1.IN2
  N6: Pico/Pico2_Mod_1.pin_11, Driver1.IN3
  N7: Pico/Pico2_Mod_1.pin_12, Driver1.IN4
  N8: Pico/Pico2_Mod_1.pin_14, Driver2.IN1
  N9: Pico/Pico2_Mod_1.pin_15, Driver2.IN2
  N10: Pico/Pico2_Mod_1.pin_16, Driver2.IN3
  N11: Pico/Pico2_Mod_1.pin_17, Driver2.IN4
  N12: Pico/Pico2_Mod_1.pin_40, ZS-042_RTC1.VCC
  GND: Driver1.GND, Driver2.GND
  N13: Driver1.Vmotor, Driver2.Vmotor
  N14: Driver1.blue-pin, SM1.blue-pin
  N15: Driver1.pink-pin, SM1.pink-pin
  N16: Driver1.yellow-pin, SM1.yellow-pin
  N17: Driver1.orange-pin, SM1.orange-pin
  N18: Driver1.red-pin, SM1.red-pin
  N19: Driver2.blue-pin, SM2.blue-pin
  N20: Driver2.pink-pin, SM2.pink-pin
  N21: Driver2.yellow-pin, SM2.yellow-pin
  N22: Driver2.orange-pin, SM2.orange-pin
  N23: Driver2.red-pin, SM2.red-pin

custom parts:
  Raspberry Pi Pico or Pico 2: Raspberry Pi Pico and Pico 2. Based around the RP2040 and RP2350 microcontrollers respectively, Picos are low cost microcontroller device bringing Raspberry Pi quality, cost, and easy of use to the microcontroller space. Jan 2021, Split part in to two versions: tht (this one) and SMD. This one will drill holes for a .1 in header in pcb to allow plugging in the module as well as providing pads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
  28BYJ-48 Driver Module: ULN2003 Driver Module for the 28BYJ-48 Unipolar Stepper Motor LED A - Blue wire - Bottom coil left LED B - Pink wire - Top coil left LED C - Yellow wire - Bottom coil right LED D - Orange wire - Top coil right Common rail - red Connector pins: blue - pink - yellow - orange - red Control pins - IN1 to IN4 Power pins - GND & Vmotor (5-12V) On/Off jumper (if removed, power to motor is cut).
  28BYJ-48 Stepper Motor: Unipolar Stepper Motor 28BYJ-48 Top coil - pink & orange Bottom coil - blue & yellow Common rail - red Connector pins: blue - pink - yellow - orange - red
